// Digital circuit controlled-reg-double-input.dig as structural Verilog
module controlled_reg_double_input (
  input  [7:0] D,
  input  C,
  input  en,
  input  [7:0] D2,
  input  Di,
  output [7:0] Q
);

  wire [7:0] driver_1_out, or_1_out;

  assign driver_1_out = Di ? D : 8'bz;  // Driver driver_1
  PullDown #(.Bits(8)) pulldown_1 (.out(driver_1_out));
  assign or_1_out = driver_1_out | D2;  // Or or_1, 8 bits wide
  Register #(.Bits(8), .isProgramCounter("true")) Reg (.D(or_1_out), .C(C), .en(en), .Q(Q));
endmodule
