// Digital circuit D-type.dig as structural Verilog
module D_type (
  input  D,
  input  Clk,
  input  Rst,
  input  Pr,
  output Q,
  output Qn
);

  wire not_1_out, not_2_out, sr_clock_1_q, sr_clock_1_qn;

  not not_1 (not_1_out, D);
  SR_clock sr_clock_1 (.S(D), .Clk(not_2_out), .R(not_1_out), .Q(sr_clock_1_q), .Qn(sr_clock_1_qn), .Pr(Pr), .Rst(Rst));
  not not_2 (not_2_out, Clk);
  SR_clock sr_clock_2 (.S(sr_clock_1_q), .Clk(Clk), .R(sr_clock_1_qn), .Q(Q), .Qn(Qn), .Pr(Pr), .Rst(Rst));
endmodule
