// Digital circuit JK-type.dig as structural Verilog
module JK_type (
  input  Clk,
  input  J,
  input  K,
  input  Rst,
  input  Pr,
  output Q,
  output Qn
);

  wire and_1_out, and_2_out, not_1_out, sr_clock_1_q, sr_clock_1_qn;

  // JK_type jk_type_1: pin names not known
  and and_1 (and_1_out, Qn, J);
  and and_2 (and_2_out, K, Q);
  SR_clock sr_clock_1 (
    .S(and_1_out), .Clk(Clk), .R(and_2_out), .Q(sr_clock_1_q), .Qn(sr_clock_1_qn), .Pr(Pr), .Rst(Rst));
  not not_1 (not_1_out, Clk);
  SR_clock sr_clock_2 (.S(sr_clock_1_q), .Clk(not_1_out), .R(sr_clock_1_qn), .Q(Q), .Qn(Qn), .Pr(Pr), .Rst(Rst));
endmodule

/* Test case:
Clk J K Rst Pr Q Qn
0 0 0 0 0 0 1
0 0 0 0 1 1 0
0 0 0 0 0 1 0
0 0 0 1 0 0 1
0 0 0 0 0 0 1
0 1 0 0 0 0 1
0 0 0 0 0 0 1
1 0 0 0 0 0 1
0 0 0 0 0 0 1
0 0 1 0 0 0 1
0 0 0 0 0 0 1
0 1 0 0 0 0 1
1 1 0 0 0 0 1
1 0 0 0 0 0 1
0 0 0 0 0 1 0
1 1 0 0 0 1 0
0 1 0 0 0 1 0
0 0 0 0 0 1 0
0 0 1 0 0 1 0
1 0 1 0 0 1 0
0 0 1 0 0 0 1
*/
