// Digital circuit SR-clock.dig as structural Verilog
// SR FlipFlop
module SR_clock (
  input  S,
  input  Clk,
  input  R,
  input  Pr,
  input  Rst,
  output Qn,
  output Q
);

  wire and_1_out, and_2_out;

  and and_1 (and_1_out, S, Clk);
  and and_2 (and_2_out, Clk, R);
  nor nor_1 (Qn, and_1_out, Pr, Q);
  nor nor_2 (Q, Qn, Rst, and_2_out);

  // Notes on the sheet:
  //   Pr: Preset forces Q to 1
  //   Rst: Reset/clear forces q to 0
endmodule
