// Digital circuit 4-bit-shift.dig as structural Verilog
module _4_bit_shift (
  input  In,
  input  Clk,
  input  Rst,
  input  Ia,
  input  Ib,
  input  Ic,
  input  Id,
  input  Pr,
  output Qa,
  output Qb,
  output Qc,
  output Qd
);

  wire or_1_out, or_2_out, or_3_out, or_4_out;

  D_type d_type_1 (.D(In), .Clk(Clk), .Q(Qa), .Rst(Rst), .Pr(or_1_out));  // open: Qn
  or or_1 (or_1_out, Ia, Pr);
  D_type d_type_2 (.D(Qa), .Clk(Clk), .Q(Qb), .Rst(Rst), .Pr(or_2_out));  // open: Qn
  or or_2 (or_2_out, Ib, Pr);
  D_type d_type_3 (.D(Qb), .Clk(Clk), .Q(Qc), .Rst(Rst), .Pr(or_3_out));  // open: Qn
  or or_3 (or_3_out, Ic, Pr);
  or or_4 (or_4_out, Id, Pr);
  D_type d_type_4 (.D(Qc), .Clk(Clk), .Q(Qd), .Rst(Rst), .Pr(or_4_out));  // open: Qn
endmodule
