// Digital circuit 8-bit-shift.dig as structural Verilog
module _8_bit_shift (
  input  In,
  input  Clk,
  input  Rst,
  input  Ia,
  input  Ib,
  input  Ic,
  input  Id,
  input  St,
  input  Ie,
  input  If,
  input  Ig,
  input  Ih,
  output Qa,
  output Qb,
  output Qc,
  output Qd,
  output Qe,
  output Qf,
  output Qg,
  output Qh
);

  wire and_1_out, and_2_out, and_3_out, and_4_out, and_5_out, and_6_out, and_7_out, and_8_out;

  D_type d_type_1 (.D(In), .Clk(Clk), .Q(Qa), .Rst(Rst), .Pr(and_1_out));  // open: Qn
  and and_1 (and_1_out, Ia, St);
  D_type d_type_2 (.D(Qa), .Clk(Clk), .Q(Qb), .Rst(Rst), .Pr(and_2_out));  // open: Qn
  and and_2 (and_2_out, Ib, St);
  D_type d_type_3 (.D(Qb), .Clk(Clk), .Q(Qc), .Rst(Rst), .Pr(and_3_out));  // open: Qn
  and and_3 (and_3_out, Ic, St);
  and and_4 (and_4_out, Id, St);
  D_type d_type_4 (.D(Qc), .Clk(Clk), .Q(Qd), .Rst(Rst), .Pr(and_4_out));  // open: Qn
  D_type d_type_5 (.D(Qd), .Clk(Clk), .Q(Qe), .Rst(Rst), .Pr(and_5_out));  // open: Qn
  and and_5 (and_5_out, Ie, St);
  D_type d_type_6 (.D(Qe), .Clk(Clk), .Q(Qf), .Rst(Rst), .Pr(and_6_out));  // open: Qn
  and and_6 (and_6_out, If, St);
  D_type d_type_7 (.D(Qf), .Clk(Clk), .Q(Qg), .Rst(Rst), .Pr(and_7_out));  // open: Qn
  and and_7 (and_7_out, Ig, St);
  and and_8 (and_8_out, Ih, St);
  D_type d_type_8 (.D(Qg), .Clk(Clk), .Q(Qh), .Rst(Rst), .Pr(and_8_out));  // open: Qn

  // Notes on the sheet:
  //   St: Set resister value
endmodule
