// Digital circuit pc-16bit.dig as structural Verilog
module pc_16bit (
  input  [15:0] D,
  input  Ct,
  input  St,
  output [15:0] Q
);

  wire or_1_out;
  wire [15:0] multiplexer_1_out, NextVal;

  Multiplexer #(.Bits(16)) multiplexer_1 (.sel(Ct), .in_0(D), .in_1(NextVal), .out(multiplexer_1_out));
  or or_1 (or_1_out, St, Ct);
  Register #(.Bits(16), .isProgramCounter("true")) register_1 (
    .D(multiplexer_1_out), .C(or_1_out), .en(or_1_out), .Q(Q));
  Add #(.Bits(16)) add_1 (.a(Q), .b(16'h1), .c_i(1'b0), .s(NextVal));  // open: c_o

  // Other names for the same wires on the sheet: Count = Ct; DataIn[15:0] = D; Store = St

  // Notes on the sheet:
  //   D: Data in
  //   Ct: Count
  //   St: Set value from D
endmodule

/* Test case:
D Ct St Q
0x0 0 0 0x0
0x0 1 0 0x1
0x0 0 0 0x1
0x0 1 0 0x2
0x0 0 0 0x2
0x0 0 1 0x0
0x0 0 0 0x0
0xa 0 0 0x0
0xa 0 1 0xa
0xa 0 0 0xa
0xa 1 0 0xb
0xa 0 0 0xb
0xffff 0 0 0xb
0xffff 0 1 0xffff
0xffff 0 0 0xffff
0xffff 1 0 0x0
0xffff 0 0 0x0
*/
