// Digital circuit edge-detect.dig as structural Verilog
module edge_detect (
  input  D,
  input  Clock,
  output Re,
  output Fe
);

  wire d_type_1_qn;

  D_type d_type_1 (.D(D), .Clk(Clock), .Qn(d_type_1_qn), .Rst(1'b0), .Pr(1'b0));  // open: Q
  and and_1 (Re, D, d_type_1_qn);
  nor nor_1 (Fe, D, d_type_1_qn);

  // Notes on the sheet:
  //   Re: Rising edge
  //   Clock: Hz: 10
  //   Fe: Falling Edge
endmodule
